// Digital circuit ControlUnit.dig as structural Verilog
module ControlUnit (
  input  [7:0] FirstByte,
  input  [7:0] SecondByte,
  input  F_Greater,
  input  F_Less,
  input  F_Equal,
  input  F_NotEqual,
  input  Clock_5,
  input  Clock_4,
  input  Clock_3,
  input  Clock_2,
  input  Clock_1,
  input  Carry,
  output D_Clk_MDR,
  output D_Clk_SRAM,
  output D_Clk_RegOutput,
  output D_Clk_RegBufferSecond,
  output D_Clk_RegBufferFirst,
  output D_Clk_Flags,
  output D_Clk_RPC,
  output D_Clk_CIRSecond,
  output D_Clk_CIRFirst,
  output D_RPC_Registers,
  output D_RPC_MemAdder,
  output D_ALU_Increment,
  output S_CTL_Halt,
  output S_ADR_Direct,
  output S_ADR_Immediate,
  output S_ALU_OrOut,
  output S_ALU_ResultOut,
  output S_ALU_Propagate,
  output S_ALU_Invert,
  output S_ALU_CarryOut,
  output S_MEM_Store,
  output S_MDR_WriteMEM,
  output S_MDR_WriteALU,
  output S_REG_WriteMDR,
  output S_REG_WriteALU
);

  wire signalintegrator_1_p11, signalintegrator_1_p12, signalintegrator_1_p13, signalintegrator_1_p15,
       signalintegrator_1_p17, signalintegrator_1_p20, signalintegrator_1_p23, signalintegrator_1_p24,
       signalintegrator_1_p25, signalintegrator_1_p26, signalintegrator_1_p28, signalintegrator_1_p30,
       signalintegrator_1_p32, staticcontrolunit_1_p4;

  // StaticControlUnit staticcontrolunit_1: pin names not known; wires that end beside it: FirstByte, SecondByte, S_CTL_Halt, staticcontrolunit_1_p4, S_ADR_Direct, S_ADR_Immediate, S_ALU_OrOut, S_ALU_ResultOut, S_ALU_Propagate, S_ALU_Invert, S_ALU_CarryOut, S_MDR_WriteMEM, S_MDR_WriteALU
  // SignalIntegrator signalintegrator_1: pin names not known; wires that end beside it: Clock_5, Clock_4, Clock_3, Clock_2, Clock_1, S_MDR_WriteMEM, S_MDR_WriteALU, S_MEM_Store, S_REG_WriteMDR, S_REG_WriteALU, signalintegrator_1_p11, signalintegrator_1_p12, signalintegrator_1_p13, F_NotEqual, signalintegrator_1_p15, F_Equal, signalintegrator_1_p17, F_Less, D_Clk_CIRFirst, signalintegrator_1_p20, F_Greater, D_RPC_Registers, signalintegrator_1_p23, signalintegrator_1_p24, signalintegrator_1_p25, signalintegrator_1_p26, D_RPC_MemAdder, signalintegrator_1_p28, Carry, signalintegrator_1_p30, D_ALU_Increment, signalintegrator_1_p32, staticcontrolunit_1_p4, signalintegrator_1_p23, signalintegrator_1_p25, signalintegrator_1_p28
endmodule
